// Digital circuit 16-bit counter.dig as structural Verilog
module _16_bit_counter (
  input  CLK,
  input  CLR,
  output [15:0] count
);

  wire [15:0] _16_bit_sum_1_sum;

  _16_bit_register _16_bit_register_1 (.D(_16_bit_sum_1_sum), .CLK(CLK), .CLR(CLR), .Q(count));  // open: nQ
  _16_bit_sum _16_bit_sum_1 (.cin(1'b0), .A(count), .B(16'h1), .sum(_16_bit_sum_1_sum));  // open: cout
endmodule
