// Digital circuit 16-bit register.dig as structural Verilog
module _16_bit_register (
  input  [15:0] D,
  input  CLK,
  input  CLR,
  output [15:0] Q,
  output [15:0] nQ
);

  _4_bit_register _4_bit_register_1 (.D(D[3:0]), .CLK(CLK), .CLR(CLR), .Q(Q[3:0]), .nQ(nQ[3:0]));
  _4_bit_register _4_bit_register_2 (.D(D[7:4]), .CLK(CLK), .CLR(CLR), .Q(Q[7:4]), .nQ(nQ[7:4]));
  _4_bit_register _4_bit_register_3 (.D(D[11:8]), .CLK(CLK), .CLR(CLR), .Q(Q[11:8]), .nQ(nQ[11:8]));
  _4_bit_register _4_bit_register_4 (.D(D[15:12]), .CLK(CLK), .CLR(CLR), .Q(Q[15:12]), .nQ(nQ[15:12]));
endmodule
