// Digital circuit 16-bit sum.dig as structural Verilog
module _16_bit_sum (
  input  cin,
  input  [15:0] A,
  input  [15:0] B,
  output [15:0] sum,
  output cout
);

  wire _4_bit_sum_1_cout, _4_bit_sum_2_cout, _4_bit_sum_3_cout;

  // Probe on cin
  _4_bit_sum _4_bit_sum_1 (.cin(cin), .B(B[3:0]), .A(A[3:0]), .sum(sum[3:0]), .cout(_4_bit_sum_1_cout));
  _4_bit_sum _4_bit_sum_2 (.cin(_4_bit_sum_1_cout), .B(B[7:4]), .A(A[7:4]), .sum(sum[7:4]), .cout(_4_bit_sum_2_cout));
  _4_bit_sum _4_bit_sum_3 (
    .cin(_4_bit_sum_2_cout), .B(B[11:8]), .A(A[11:8]), .sum(sum[11:8]), .cout(_4_bit_sum_3_cout));
  _4_bit_sum _4_bit_sum_4 (.cin(_4_bit_sum_3_cout), .B(B[15:12]), .A(A[15:12]), .sum(sum[15:12]), .cout(cout));
  // Probe on cout
endmodule
