// Digital circuit 4-bit register.dig as structural Verilog
module _4_bit_register (
  input  [3:0] D,
  input  CLK,
  input  CLR,
  output [3:0] Q,
  output [3:0] nQ
);

  D_flip_flop d_flip_flop_1 (.D(D[0]), .CLK(CLK), .CLR(CLR), .Q(Q[0]), .nQ(nQ[0]));
  D_flip_flop d_flip_flop_2 (.D(D[1]), .CLK(CLK), .CLR(CLR), .Q(Q[1]), .nQ(nQ[1]));
  D_flip_flop d_flip_flop_3 (.D(D[2]), .CLK(CLK), .CLR(CLR), .Q(Q[2]), .nQ(nQ[2]));
  D_flip_flop d_flip_flop_4 (.D(D[3]), .CLK(CLK), .CLR(CLR), .Q(Q[3]), .nQ(nQ[3]));
endmodule
