// Digital circuit 4-bit sum.dig as structural Verilog
module _4_bit_sum (
  input  cin,
  input  [3:0] B,
  input  [3:0] A,
  output [3:0] sum,
  output cout
);

  wire sum_1_cout, sum_2_cout, sum_3_cout;

  // Probe on cin
  sum sum_1 (.a(A[0]), .b(B[0]), .cin(cin), .sum(sum[0]), .cout(sum_1_cout));
  sum sum_2 (.a(A[1]), .b(B[1]), .cin(sum_1_cout), .sum(sum[1]), .cout(sum_2_cout));
  sum sum_3 (.a(A[2]), .b(B[2]), .cin(sum_2_cout), .sum(sum[2]), .cout(sum_3_cout));
  sum sum_4 (.a(A[3]), .b(B[3]), .cin(sum_3_cout), .sum(sum[3]), .cout(cout));
  // Probe on cout
endmodule
