// Digital circuit 8-to-1 multiplexors.dig as structural Verilog
module _8_to_1_multiplexors (
  input  [2:0] s,
  input  a0,
  input  a1,
  input  a2,
  input  a3,
  input  a4,
  input  a5,
  input  a6,
  input  a7,
  output out
);

  wire and_1_out, and_2_out, and_3_out, and_4_out, and_5_out, and_6_out, and_7_out, and_8_out;

  and and_1 (and_1_out, ~s[0], ~s[1], ~s[2], a0);  // And
  and and_2 (and_2_out, s[0], ~s[1], ~s[2], a1);  // And
  and and_3 (and_3_out, ~s[0], s[1], ~s[2], a2);  // And
  and and_4 (and_4_out, s[0], s[1], ~s[2], a3);  // And
  and and_5 (and_5_out, ~s[0], ~s[1], s[2], a4);  // And
  and and_6 (and_6_out, s[0], ~s[1], s[2], a5);  // And
  and and_7 (and_7_out, ~s[0], s[1], s[2], a6);  // And
  and and_8 (and_8_out, s[0], s[1], s[2], a7);
  or or_1 (out, and_1_out, and_2_out, and_3_out, and_4_out, and_5_out, and_6_out, and_7_out, and_8_out);
endmodule
