// Digital circuit D flip-flop.dig as structural Verilog
module D_flip_flop (
  input  D,
  input  CLK,
  input  CLR,
  output Q,
  output nQ
);

  wire d_latch_1_q, not_1_out;

  not not_1 (not_1_out, CLK);
  D_Latch d_latch_1 (.CLR(CLR), .CLK(not_1_out), .D(D), .Q(d_latch_1_q));  // open: nQ
  D_Latch d_latch_2 (.CLR(CLR), .CLK(CLK), .D(d_latch_1_q), .Q(Q), .nQ(nQ));
endmodule
