// Digital circuit controler.dig as structural Verilog
module controler (
  input  [15:0] counter_input,
  output [2:0] MUX_S,
  output [4:0] ROM_A,
  output [6:0] RAM_A,
  output RAM_B
);

  not not_1 (RAM_B, counter_input[6]);
  // Pins of 1 and 16 bits meet at counter_input
  // Pins of 1 and 3 bits meet at counter_input[2:0]
  // Pins of 1 and 5 bits meet at counter_input[7:3]
  // Pins of 1 and 7 bits meet at counter_input[6:0]

  assign MUX_S = counter_input[2:0];
  assign RAM_A = counter_input[6:0];
  assign ROM_A = counter_input[7:3];
endmodule
