// Digital circuit main.dig as structural Verilog
module main (
  input  in_1,
  input  clk
);

  wire _8_to_1_multiplexors_1_p10, _16_bit_counter_1_p3, controler_1_p2, controler_1_p4, controler_1_p5;
  wire [4:0] controler_1_p3;
  wire [7:0] rom_1_d;

  // _16_bit_counter _16_bit_counter_1: pin names not known; wires that end beside it: clk, in_1, _16_bit_counter_1_p3
  // controler controler_1: pin names not known; wires that end beside it: _16_bit_counter_1_p3, controler_1_p2, controler_1_p3, controler_1_p4, controler_1_p5
  ROM #(.AddrBits(5), .Bits(8)) rom_1 (.A(controler_1_p3), .sel(1'b1), .D(rom_1_d));
  // _8_to_1_multiplexors _8_to_1_multiplexors_1: pin names not known; wires that end beside it: controler_1_p2, rom_1_d[7], rom_1_d[6], rom_1_d[5], rom_1_d[4], rom_1_d[3], rom_1_d[2], rom_1_d[1], rom_1_d[0], _8_to_1_multiplexors_1_p10
  GraphicCard #(.graphicHeight(8), .graphicWidth(8)) graphiccard_1 (
    .A(controler_1_p4), .str(1'b1), .C(clk), .ld(1'b0), .B(controler_1_p5), .D(_8_to_1_multiplexors_1_p10));

  // Notes on the sheet:
  //   clk: Hz: 100
  //   contents of rom_1 (hex, n*v repeats v):
  //   0,0,0,ff,ff,0,0,0,18,18,18,ff,ff,18,18,18,98,58,38,ff,ff,1c,1a,19,99,5a,3c,ff,ff,
  //   3c,5a,99
endmodule
