// Digital circuit Main-decoder.dig as structural Verilog
module Main_decoder (
  input  [31:0] iw,
  output RFW,
  output [1:0] EXT,
  output [1:0] ALUop,
  output ALU1src,
  output CMP,
  output MUL,
  output STR,
  output LDR,
  output BX,
  output BR,
  output BL
);

  wire add_i, add_r, cmp_i, cmp_r, comparator_2_eq, comparator_3_eq, comparator_4_eq, comparator_5_eq,
       comparator_6_eq, comparator_7_eq, comparator_8_eq, mov_i, mov_r, or_1_out, or_2_out, or_3_out,
       or_4_out, sub_i, sub_r;

  // Probe on iw
  Comparator #(.Bits(24)) comparator_1 (.a(iw[27:4]), .b(24'h12fff1), .eq(BX));  // open: gt, lt
  Comparator #(.Bits(4)) comparator_2 (.a(iw[7:4]), .b(4'b1001), .eq(comparator_2_eq));  // open: gt, lt
  Comparator #(.Bits(6)) comparator_3 (.a(iw[27:22]), .b({6{1'b0}}), .eq(comparator_3_eq));  // open: gt, lt
  Comparator #(.Bits(2)) comparator_4 (.a(iw[27:26]), .b(2'b01), .eq(comparator_4_eq));  // open: gt, lt
  Comparator #(.Bits(4)) comparator_5 (.a(iw[24:21]), .b(4'b0100), .eq(comparator_5_eq));  // open: gt, lt
  Comparator #(.Bits(4)) comparator_6 (.a(iw[24:21]), .b(4'b1101), .eq(comparator_6_eq));  // open: gt, lt
  Comparator #(.Bits(4)) comparator_7 (.a(iw[24:21]), .b(4'b0010), .eq(comparator_7_eq));  // open: gt, lt
  Comparator #(.Bits(4)) comparator_8 (.a(iw[24:21]), .b(4'b1010), .eq(comparator_8_eq));  // open: gt, lt
  and and_1 (LDR, iw[20], comparator_4_eq);
  and and_2 (STR, comparator_4_eq, ~iw[20]);  // And
  and and_3 (MUL, comparator_2_eq, comparator_3_eq);
  and and_4 (add_r, ~iw[27], ~iw[26], ~iw[25], comparator_5_eq);  // And
  and and_5 (add_i, ~iw[27], ~iw[26], iw[25], comparator_5_eq);  // And
  and and_6 (mov_r, ~iw[27], ~iw[26], ~iw[25], comparator_6_eq);  // And
  and and_7 (mov_i, ~iw[27], ~iw[26], iw[25], comparator_6_eq);  // And
  and and_8 (sub_r, ~iw[27], ~iw[26], ~iw[25], comparator_7_eq);  // And
  and and_9 (sub_i, ~iw[27], ~iw[26], iw[25], comparator_7_eq);  // And
  and and_10 (cmp_r, ~iw[27], ~iw[26], ~iw[25], comparator_8_eq);  // And
  and and_11 (cmp_i, ~iw[27], ~iw[26], iw[25], comparator_8_eq);  // And
  and and_12 (BR, iw[27], ~iw[26], iw[25]);  // And
  and and_13 (BL, BR, iw[24]);
  or or_1 (or_1_out, add_r, add_i, sub_r, sub_i, mov_r, mov_i, BL, MUL, LDR);
  or or_2 (or_2_out, mov_i, mov_r, cmp_r, cmp_i, sub_r, sub_i);
  or or_3 (or_3_out, mov_i, MUL, mov_r);
  or or_4 (or_4_out, add_i, sub_i, BR, mov_i, cmp_i, LDR, STR);
  or or_5 (RFW, or_1_out, 1'b0);
  or or_6 (EXT[0], STR, LDR);
  or or_7 (EXT[1], BR, 1'b0);
  or or_8 (ALUop[0], or_2_out, 1'b0);
  or or_9 (ALUop[1], or_3_out, 1'b0);
  or or_10 (ALU1src, or_4_out, 1'b0);
  or or_11 (CMP, cmp_i, cmp_r);

  // Other names for the same wires on the sheet: b_offset[23:0] = iw[23:0]; imm[7:0] = iw[7:0];
  //   immoff[11:0] = iw[11:0]; rm[3:0] = iw[3:0]; rm_mul[3:0] = iw[3:0]; bxcode[23:0] = iw[27:4];
  //   opmul4[3:0] = iw[7:4]; rs_mul[3:0] = iw[11:8]; rd[3:0] = iw[15:12]; rn_mul[3:0] = iw[15:12];
  //   rd_mul[3:0] = iw[19:16]; rn[3:0] = iw[19:16]; l_sdt = iw[20]; s_dp = iw[20]; s_mul = iw[20]; a_mul = iw[21];
  //   opc[3:0] = iw[24:21]; w_sdt = iw[21]; b_sdt = iw[22]; opmul6[5:0] = iw[27:22]; u_sdt = iw[23]; l_b = iw[24];
  //   p_sdt = iw[24]; i_sdt = iw[25]; op0 = iw[25]; op0_i_dp = iw[25]; op1 = iw[26]; opmul2[1:0] = iw[27:26];
  //   op2 = iw[27]; cond[3:0] = iw[31:28]; ldr_i = LDR; mul_r = MUL; str_i = STR

  // Notes on the sheet:
  //   mul(r)
  //   ldr(i)
  //   str(i)
  //   add(r)
  //   add(i)
  //   mov(r)
  //   mov(i)
  //   sub(r)
  //   sub(i)
  //   cmp(r)
  //   cmp(i)
  //   b
  //   bl
endmodule
