// Digital circuit RegParser.dig as structural Verilog
module RegParser (
  input  [31:0] IW,
  input  BR,
  input  BL,
  input  MUL,
  input  STR,
  output [3:0] ReadReg1,
  output [3:0] WriteReg,
  output [3:0] ReadReg0
);

  wire [3:0] multiplexer_1_out, multiplexer_2_out, multiplexer_3_out;

  Multiplexer #(.Bits(4)) multiplexer_1 (.sel(STR), .in_0(IW[3:0]), .in_1(IW[15:12]), .out(multiplexer_1_out));
  Multiplexer #(.Bits(4)) multiplexer_2 (.sel(BR), .in_0(IW[19:16]), .in_1(4'b1111), .out(multiplexer_2_out));
  Multiplexer #(.Bits(4)) multiplexer_3 (.sel(BL), .in_0(IW[15:12]), .in_1(4'b1110), .out(multiplexer_3_out));
  Multiplexer #(.Bits(4)) multiplexer_4 (.sel(MUL), .in_0(multiplexer_2_out), .in_1(IW[3:0]), .out(ReadReg0));
  Multiplexer #(.Bits(4)) multiplexer_5 (.sel(MUL), .in_0(multiplexer_1_out), .in_1(IW[11:8]), .out(ReadReg1));
  Multiplexer #(.Bits(4)) multiplexer_6 (.sel(MUL), .in_0(multiplexer_3_out), .in_1(IW[19:16]), .out(WriteReg));

  // Notes on the sheet:
  //   DP/B
  //   MUL
  //   Rm
  //   Rn
  //   Rd
  //   Rs
endmodule
