// Digital circuit RegisterFile.dig as structural Verilog
module RegisterFile (
  input  [3:0] ReadReg0,
  input  [3:0] ReadReg1,
  input  [3:0] WriteReg,
  input  [31:0] WriteData,
  input  WriteEN,
  input  [31:0] PC,
  input  CLK,
  output [31:0] RD0,
  output [31:0] RD1,
  output [31:0] r0,
  output [31:0] r1,
  output [31:0] r2,
  output [31:0] r3,
  output [31:0] r4,
  output [31:0] r5,
  output [31:0] r6,
  output [31:0] r7,
  output [31:0] r8,
  output [31:0] r9,
  output [31:0] r10,
  output [31:0] r11,
  output [31:0] r12,
  output [31:0] r13,
  output [31:0] r14,
  output [31:0] r15
);

  wire and_1_out, and_2_out, and_3_out, and_4_out, and_5_out, and_6_out, and_7_out, and_8_out, and_9_out,
       and_10_out, and_11_out, and_12_out, and_13_out, and_14_out, and_15_out, decoder_1_out_0,
       decoder_1_out_1, decoder_1_out_2, decoder_1_out_3, decoder_1_out_4, decoder_1_out_5, decoder_1_out_6,
       decoder_1_out_7, decoder_1_out_8, decoder_1_out_9, decoder_1_out_10, decoder_1_out_11,
       decoder_1_out_12, decoder_1_out_13, decoder_1_out_14, decoder_1_out_15;

  Decoder #(.Selector_Bits(4)) decoder_1 (
    .sel(WriteReg), .out_0(decoder_1_out_0), .out_1(decoder_1_out_1), .out_2(decoder_1_out_2),
    .out_3(decoder_1_out_3), .out_4(decoder_1_out_4), .out_5(decoder_1_out_5), .out_6(decoder_1_out_6),
    .out_7(decoder_1_out_7), .out_8(decoder_1_out_8), .out_9(decoder_1_out_9), .out_10(decoder_1_out_10),
    .out_11(decoder_1_out_11), .out_12(decoder_1_out_12), .out_13(decoder_1_out_13),
    .out_14(decoder_1_out_14), .out_15(decoder_1_out_15));
  and and_1 (and_1_out, decoder_1_out_0, WriteEN);
  and and_2 (and_2_out, decoder_1_out_1, WriteEN);
  and and_3 (and_3_out, decoder_1_out_2, WriteEN);
  and and_4 (and_4_out, decoder_1_out_3, WriteEN);
  and and_5 (and_5_out, decoder_1_out_4, WriteEN);
  and and_6 (and_6_out, decoder_1_out_5, WriteEN);
  and and_7 (and_7_out, decoder_1_out_6, WriteEN);
  and and_8 (and_8_out, decoder_1_out_7, WriteEN);
  and and_9 (and_9_out, decoder_1_out_8, WriteEN);
  and and_10 (and_10_out, decoder_1_out_9, WriteEN);
  and and_11 (and_11_out, decoder_1_out_10, WriteEN);
  and and_12 (and_12_out, decoder_1_out_11, WriteEN);
  and and_13 (and_13_out, decoder_1_out_12, WriteEN);
  and and_14 (and_14_out, decoder_1_out_13, WriteEN);
  and and_15 (and_15_out, decoder_1_out_14, WriteEN);
  Register #(.Bits(32)) u_r0 (.D(WriteData), .C(CLK), .en(and_1_out), .Q(r0));
  Register #(.Bits(32)) u_r1 (.D(WriteData), .C(CLK), .en(and_2_out), .Q(r1));
  Register #(.Bits(32)) u_r2 (.D(WriteData), .C(CLK), .en(and_3_out), .Q(r2));
  Register #(.Bits(32)) u_r3 (.D(WriteData), .C(CLK), .en(and_4_out), .Q(r3));
  Register #(.Bits(32)) u_r4 (.D(WriteData), .C(CLK), .en(and_5_out), .Q(r4));
  Register #(.Bits(32)) u_r5 (.D(WriteData), .C(CLK), .en(and_6_out), .Q(r5));
  Register #(.Bits(32)) u_r6 (.D(WriteData), .C(CLK), .en(and_7_out), .Q(r6));
  Register #(.Bits(32)) u_r7 (.D(WriteData), .C(CLK), .en(and_8_out), .Q(r7));
  Register #(.Bits(32)) u_r8 (.D(WriteData), .C(CLK), .en(and_9_out), .Q(r8));
  Register #(.Bits(32)) u_r9 (.D(WriteData), .C(CLK), .en(and_10_out), .Q(r9));
  Register #(.Bits(32)) u_r10 (.D(WriteData), .C(CLK), .en(and_11_out), .Q(r10));
  Register #(.Bits(32)) u_r11 (.D(WriteData), .C(CLK), .en(and_12_out), .Q(r11));
  Register #(.Bits(32)) u_r12 (.D(WriteData), .C(CLK), .en(and_13_out), .Q(r12));
  Register #(.Bits(32)) u_r13 (.D(WriteData), .C(CLK), .en(and_14_out), .Q(r13));
  Register #(.Bits(32)) u_r14 (.D(WriteData), .C(CLK), .en(and_15_out), .Q(r14));
  Multiplexer #(.Selector_Bits(4), .Bits(32)) multiplexer_1 (
    .sel(ReadReg0), .in_0(r0), .in_1(r1), .in_2(r2), .in_3(r3), .in_4(r4), .in_5(r5), .in_6(r6), .in_7(r7),
    .in_8(r8), .in_9(r9), .in_10(r10), .in_11(r11), .in_12(r12), .in_13(r13), .in_14(r14), .in_15(PC),
    .out(RD0));
  Multiplexer #(.Selector_Bits(4), .Bits(32)) multiplexer_2 (
    .sel(ReadReg1), .in_0(r0), .in_1(r1), .in_2(r2), .in_3(r3), .in_4(r4), .in_5(r5), .in_6(r6), .in_7(r7),
    .in_8(r8), .in_9(r9), .in_10(r10), .in_11(r11), .in_12(r12), .in_13(r13), .in_14(r14), .in_15(PC),
    .out(RD1));

  assign r15 = PC;
endmodule
