// Digital circuit control_unit_conditional.dig as structural Verilog
module control_unit_conditional (
  input  [31:0] iw,
  input  [3:0] NZCV,
  input  CLK,
  output RFW,
  output [1:0] EXT,
  output [1:0] ALUop,
  output ALU1src,
  output BR,
  output BX,
  output MUL,
  output STR,
  output LDR,
  output BL
);

  wire AL_eq, and_1_out, and_2_out, and_3_out, C, comparator_1_eq, comparator_2_eq, comparator_3_eq, EQ_eq,
       GE_eq, GT_eq, main_decoder_1_br, main_decoder_1_cmp, N, or_1_out, V, Z;

  Main_decoder main_decoder_1 (
    .iw(iw), .RFW(RFW), .EXT(EXT), .ALUop(ALUop), .ALU1src(ALU1src), .MUL(MUL), .STR(STR), .LDR(LDR),
    .BX(BX), .BL(BL), .BR(main_decoder_1_br), .CMP(main_decoder_1_cmp));
  Register #(.Bits(4)) register_1 (.D(NZCV), .C(CLK), .en(main_decoder_1_cmp), .Q({V, C, Z, N}));
  Comparator #(.Bits(4)) EQ (.a(iw[31:28]), .b(4'b0000), .eq(EQ_eq));  // open: gt, lt
  Comparator #(.Bits(4)) AL (.a(iw[31:28]), .b(4'b1110), .eq(AL_eq));  // open: gt, lt
  Comparator #(.Bits(4)) GT (.a(iw[31:28]), .b(4'b1100), .eq(GT_eq));  // open: gt, lt
  Comparator comparator_1 (.a(1'b0), .b(Z), .eq(comparator_1_eq));  // open: gt, lt
  Comparator comparator_2 (.a(V), .b(N), .eq(comparator_2_eq));  // open: gt, lt
  Comparator #(.Bits(4)) GE (.a(iw[31:28]), .b(4'b1010), .eq(GE_eq));  // open: gt, lt
  Comparator comparator_3 (.a(V), .b(N), .eq(comparator_3_eq));  // open: gt, lt
  and and_1 (and_1_out, EQ_eq, Z);
  and and_2 (and_2_out, GT_eq, comparator_1_eq, comparator_2_eq);
  and and_3 (and_3_out, GE_eq, comparator_3_eq);
  or or_1 (or_1_out, and_1_out, AL_eq, and_2_out, and_3_out);
  and and_4 (BR, main_decoder_1_br, or_1_out);
endmodule
