// Digital circuit extension-unit.dig as structural Verilog
module extension_unit (
  input  [31:0] iw,
  input  [1:0] EXT,
  output [31:0] exitimm
);

  Multiplexer #(.Selector_Bits(2), .Bits(32)) multiplexer_1 (
    .sel(EXT), .in_0({{24{1'b0}}, iw[7:0]}), .in_1({{20{1'b0}}, iw[11:0]}),
    .in_2({{7{iw[23]}}, iw[22:0], 2'b00}), .in_3(32'h1), .out(exitimm));

  // Notes on the sheet:
  //   immediate value(DP)
  //   immediate offset(ldr/sdr)
  //   branch offset
endmodule
