// Digital circuit first.dig as structural Verilog
module first (
  input  clk,
  input  [3:0] PN
);

  wire a_mul, ALU1src, BL, BR, BX, C, CLK_t, comparator_1_eq, dipswitch_1_out, LDR, MUL, N, r0, r1, r2, r3,
       r4, r5, r6, r7, r8, r9, r10, r11, r12, r13, r14, r15, registerfile_1_p8, regparser_1_p6,
       regparser_1_p7, regparser_1_p8, RFW, STR, V, Z;
  wire [1:0] ALUop, EXT;
  wire [3:0] alu_1_p5, cond;
  wire [23:0] b_offset;
  wire [23:20] bxcode;
  wire [31:0] add_1_s, add_2_s, alu_1_p4, extension_unit_1_exitimm, multiplexer_2_out, multiplexer_3_out,
       multiplexer_4_out, pc_in, pc_out, ramdualport_1_d, registerfile_1_p9;

  DipSwitch dipswitch_1 (.out(dipswitch_1_out));
  and and_1 (CLK_t, clk, dipswitch_1_out);
  Multiplexer #(.Selector_Bits(2), .Bits(32)) multiplexer_1 (
    .sel({BX, BR}), .in_0(add_1_s), .in_1(alu_1_p4), .in_2(registerfile_1_p9), .in_3({32{1'b0}}), .out(pc_in));
  control_unit_conditional control_unit_conditional_1 (
    .iw({cond, bxcode, b_offset[23:22], a_mul, b_offset[20:0]}), .NZCV(alu_1_p5), .CLK(CLK_t), .RFW(RFW),
    .EXT(EXT), .ALUop(ALUop), .ALU1src(ALU1src), .BR(BR), .BX(BX), .MUL(MUL), .STR(STR), .LDR(LDR), .BL(BL));
  Register #(.Bits(32)) PC (.D(pc_in), .C(CLK_t), .en(1'b1), .Q(pc_out));
  // Probe on {cond, bxcode, b_offset[23:22], a_mul, b_offset[20:0]}
  // instruction_memory instruction_memory_1: pin names not known; wires that end beside it: pc_out[7:2], 1'b1, PN, {cond, bxcode, b_offset[23:22], a_mul, b_offset[20:0]}
  Add #(.Bits(32)) add_1 (.a(pc_out), .b(32'h4), .c_i(1'b0), .s(add_1_s));  // open: c_o
  Add #(.Bits(32)) add_2 (.a(add_1_s), .b(32'h4), .c_i(1'b0), .s(add_2_s));  // open: c_o
  // RegParser regparser_1: pin names not known; wires that end beside it: STR, BR, BL, MUL, {cond, bxcode, b_offset[23:22], a_mul, b_offset[20:0]}, regparser_1_p6, regparser_1_p7, regparser_1_p8
  // Probe on r0
  // Probe on r1
  // Probe on r2
  // Probe on r3
  // Probe on cond
  // Probe on cond
  // Probe on cond
  // Probe on cond
  Multiplexer #(.Bits(32)) multiplexer_2 (.sel(BL), .in_0(alu_1_p4), .in_1(add_1_s), .out(multiplexer_2_out));
  // Probe on bxcode[23]
  // Probe on {bxcode, b_offset[23]}
  // Probe on bxcode[23:22]
  // Probe on bxcode[21]
  // Probe on regparser_1_p6
  // Probe on regparser_1_p7
  // Probe on regparser_1_p8
  Multiplexer #(.Bits(32)) multiplexer_3 (
    .sel(LDR), .in_0(multiplexer_2_out), .in_1(ramdualport_1_d), .out(multiplexer_3_out));
  // Probe on r4
  // Probe on r5
  // Probe on r6
  // Probe on r7
  // Probe on bxcode[21]
  // Probe on r8
  // Probe on r9
  // Probe on r10
  // Probe on r11
  // Probe on a_mul
  // Probe on bxcode[21]
  // Probe on bxcode[20]
  // RegisterFile registerfile_1: pin names not known; wires that end beside it: regparser_1_p6, regparser_1_p7, regparser_1_p8, multiplexer_3_out, RFW, CLK_t, add_2_s, registerfile_1_p8, registerfile_1_p9, r0, r1, r2, r3, r4, r5, r6, r7, r8, r9, r10, r11, r12, r13, r14, r15
  // Probe on {bxcode[20], b_offset[23:22], a_mul}
  // Probe on b_offset[20]
  // Probe on bxcode[20]
  // Probe on {b_offset[23:22], a_mul, b_offset[20:0]}
  // Probe on r12
  // Probe on r13
  // Probe on r14
  // Probe on r15
  // Probe on pc_out
  // Probe on b_offset[20]
  // Probe on b_offset[19:16]
  // Probe on b_offset[23]
  // Probe on N
  // Probe on Z
  // Probe on C
  // Probe on V
  // Probe on b_offset[19:16]
  // Probe on b_offset[15:12]
  // Probe on b_offset[15:12]
  // Probe on b_offset[22]
  // Probe on b_offset[11:8]
  // Probe on a_mul
  Multiplexer #(.Bits(32)) multiplexer_4 (
    .sel(ALU1src), .in_0(registerfile_1_p9), .in_1(extension_unit_1_exitimm), .out(multiplexer_4_out));
  // Probe on b_offset[3:0]
  // Probe on b_offset[7:0]
  // Probe on b_offset[7:4]
  // Probe on b_offset[20]
  extension_unit extension_unit_1 (
    .iw({cond, bxcode, b_offset[23:22], a_mul, b_offset[20:0]}), .EXT(EXT), .exitimm(extension_unit_1_exitimm));
  // Probe on b_offset[3:0]
  // Probe on b_offset[19:16]
  Comparator #(.Bits(32)) comparator_1 (.a(pc_in), .b(pc_out), .eq(comparator_1_eq));  // open: gt, lt
  // Probe on b_offset[15:12]
  // ALU alu_1: pin names not known; wires that end beside it: registerfile_1_p8, multiplexer_4_out, ALUop, alu_1_p4, alu_1_p5, N, Z, C, V
  LED led_1 (.in(comparator_1_eq));
  // Probe on b_offset[3:0]
  // Probe on extension_unit_1_exitimm
  // Probe on b_offset[11:0]
  RAMDualPort #(.AddrBits(8), .Bits(32)) ramdualport_1 (
    .A(alu_1_p4[9:2]), .Din(registerfile_1_p9), .str(STR), .C(CLK_t), .ld(LDR), .D(ramdualport_1_d));

  // Other names for the same wires on the sheet: imm[7:0] = b_offset[7:0]; immoff[11:0] = b_offset[11:0];
  //   iw[31:0] = {cond, bxcode, b_offset[23:22], a_mul, b_offset[20:0]}; rm[3:0] = b_offset[3:0];
  //   rm_mul[3:0] = b_offset[3:0]; bxcode[19:0] = {b_offset[23:22], a_mul, b_offset[20:4]};
  //   opmul4[3:0] = b_offset[7:4]; rs_mul[3:0] = b_offset[11:8]; rd[3:0] = b_offset[15:12];
  //   rn_mul[3:0] = b_offset[15:12]; rd_mul[3:0] = b_offset[19:16]; rn[3:0] = b_offset[19:16]; l_sdt = b_offset[20];
  //   s_dp = b_offset[20]; s_mul = b_offset[20]; b_offset[21] = a_mul;
  //   opc[3:0] = {bxcode[20], b_offset[23:22], a_mul}; w_sdt = a_mul; b_sdt = b_offset[22];
  //   opmul6[4:0] = {bxcode, b_offset[23]}; u_sdt = b_offset[23]; l_b = bxcode[20]; p_sdt = bxcode[20];
  //   i_dp = bxcode[21]; i_sdt = bxcode[21]; opb3 = bxcode[21]; op1 = bxcode[22]; opmul2[1:0] = bxcode[23:22];
  //   op2 = bxcode[23]

  // Notes on the sheet:
  //   clk: Hz: 2147483647
endmodule
