// Digital circuit instruction_memory.dig as structural Verilog
module instruction_memory (
  input  [31:0] A,
  input  [3:0] PN,
  output [31:0] D
);

  wire [31:0] fib_iter_10_d, fib_iter_19_d, fib_rec_10_d, fib_rec_19_d, find_max_d, quadratic_d, sum_array_d;

  ROM #(.AddrBits(6), .Bits(32)) quadratic (.A(A[5:0]), .sel(1'b1), .D(quadratic_d));
  ROM #(.AddrBits(6), .Bits(32)) find_max (.A(A[5:0]), .sel(1'b1), .D(find_max_d));
  ROM #(.AddrBits(6), .Bits(32)) sum_array (.A(A[5:0]), .sel(1'b1), .D(sum_array_d));
  ROM #(.AddrBits(6), .Bits(32)) fib_iter_10 (.A(A[5:0]), .sel(1'b1), .D(fib_iter_10_d));
  ROM #(.AddrBits(6), .Bits(32)) fib_rec_10 (.A(A[5:0]), .sel(1'b1), .D(fib_rec_10_d));
  ROM #(.AddrBits(6), .Bits(32)) fib_iter_19 (.A(A[5:0]), .sel(1'b1), .D(fib_iter_19_d));
  ROM #(.AddrBits(6), .Bits(32)) fib_rec_19 (.A(A[5:0]), .sel(1'b1), .D(fib_rec_19_d));
  Multiplexer #(.Selector_Bits(4), .Bits(32)) multiplexer_1 (
    .sel(PN), .in_0(quadratic_d), .in_1(find_max_d), .in_2(sum_array_d), .in_3(fib_iter_10_d),
    .in_4(fib_rec_10_d), .in_5(fib_iter_19_d), .in_6(fib_rec_19_d), .in_7({32{1'b0}}), .in_8({32{1'b0}}),
    .in_9({32{1'b0}}), .in_10({32{1'b0}}), .in_11({32{1'b0}}), .in_12({32{1'b0}}), .in_13({32{1'b0}}),
    .in_14({32{1'b0}}), .in_15({32{1'b0}}), .out(D));
  // Pins of 6 and 32 bits meet at A

  // Notes on the sheet:
  //   contents of quadratic (hex, n*v repeats v):
  //   e3a00002,e3a01006,e3a02007,e3a03009,eb000000,eafffffe,e0020290,e00c0090,e000019c,
  //   e0800002,e0800003,e12fff1e
  //   contents of find_max (hex, n*v repeats v):
  //   e3a0dc01,e24dd018,e3a00002,e58d0000,e3a00004,e58d0004,e3a00006,e58d0008,e3a00007,
  //   e58d000c,e3a00009,e58d0010,e1a0000d,e3a01005,eb000000,eafffffe,e3a02000,e5903000,
  //   e1520001,a000007,e590c000,e15c0003,ca000002,e2822001,e2800004,eafffff7,e1a0300c,eafffffa,
  //   e1a00003,e12fff1e
  //   contents of sum_array (hex, n*v repeats v):
  //   e3a0dc01,e24dd014,e3a00002,e58d0000,e3a00004,e58d0004,e3a00006,e58d0008,e3a00007,
  //   e58d000c,e3a00009,e58d0010,e1a0000d,e3a01005,eb000000,eafffffe,e3a02000,e3a03000,
  //   e1520001,a000004,e590c000,e083300c,e2822001,e2800004,eafffff8,e1a00003,e12fff1e
  //   contents of fib_iter_10 (hex, n*v repeats v):
  //   e3a0dc01,e3a0000a,eb000000,eafffffe,e3a01000,e3a02000,e3a03001,e3a0c001,e3500000,
  //   a000006,e15c0000,a000005,e1a01002,e1a02003,e0813002,e28cc001,eafffff8,e3a03000,e1a00003,
  //   e12fff1e
  //   contents of fib_rec_10 (hex, n*v repeats v):
  //   e3a0dc02,e3a0000a,eb000000,eafffffe,e3500000,a000012,e3500001,a00000f,e24dd008,e58de000,
  //   e58d0004,e2400001,ebfffff6,e1a01000,e59d0004,e58d1004,e2400002,ebfffff1,e1a02000,
  //   e59d1004,e0820001,e59de000,e28dd008,ea000000,e3a00001,e12fff1e
  //   contents of fib_iter_19 (hex, n*v repeats v):
  //   e3a00013,eb000000,eafffffe,e3a01000,e3a02000,e3a03001,e3a0c001,e3500000,a000006,e15c0000,
  //   a000005,e1a01002,e1a02003,e0813002,e28cc001,eafffff8,e3a03000,e1a00003,e12fff1e
  //   contents of fib_rec_19 (hex, n*v repeats v):
  //   e3a00013,e3a0dc02,eb000000,eafffffe,e3500000,a000011,e3500001,a000011,e24dd008,e58de000,
  //   e58d0004,e2400001,ebfffff6,e1a01000,e59d0004,e58d1004,e2400002,ebfffff1,e1a02000,
  //   e59d1004,e0820001,e59de000,e28dd008,ea000002,e3a00000,ea000000,e3a00001,e12fff1e
endmodule
